# Fritzing sketch layout (saved by Fritzing 0.9.3b)
breadboards: 1

parts:
  Part1 = Arduino Uno (Rev3) - ICSP
  R1 = Resistor [tolerance=±1% resistance=82 package=THT]
  R2 = Resistor [tolerance=±1% resistance=82 package=THT]
  R3 = Resistor [tolerance=±1% resistance=82 package=THT]
  R4 = Resistor [tolerance=±1% resistance=82 package=THT]
  R5 = Resistor [tolerance=±1% resistance=82 package=THT]
  R6 = Resistor [tolerance=±1% resistance=82 package=THT]
  R7 = Resistor [tolerance=±1% resistance=82 package=THT]
  R8 = Resistor [tolerance=±1% resistance=164 package=THT]
  R9 = Resistor [tolerance=±1% resistance=164 package=THT]
  R10 = Resistor [tolerance=±1% resistance=164 package=THT]
  R11 = Resistor [tolerance=±1% resistance=164 package=THT]
  R12 = Resistor [tolerance=±1% resistance=164 package=THT]
  R13 = Resistor [tolerance=±1% resistance=164 package=THT]
  R14 = Resistor [tolerance=±1% resistance=164 package=THT]
  R15 = Resistor [tolerance=±1% resistance=164 package=THT]
  R16 = Resistor [tolerance=±1% resistance=164 package=THT]
  C1 = Electrolytic Capacitor [capacitance=220µF voltage=50V package="1010 [SMD, electrolytic]"]
  SP1 = SPEAKER [package=pcb_mount_speaker]

nets:
  N1: Part1.D0/RX, R16.Pin_1
  N2: Part1.D1/TX, R15.Pin_1
  N3: Part1.D2, R14.Pin_1
  N4: Part1.D3_PWM, R13.Pin_1
  N5: Part1.D4, R12.Pin_1
  N6: Part1.D5_PWM, R11.Pin_1
  N7: Part1.D6_PWM, R10.Pin_1
  N8: Part1.D7, R8.Pin_1
  N9: Part1.GND, R9.Pin_0, SP1.+
  N10: R1.Pin_0, R8.Pin_0, C1.+
  N11: R1.Pin_1, R2.Pin_0, R10.Pin_0
  N12: R2.Pin_1, R3.Pin_0, R11.Pin_0
  N13: R3.Pin_1, R4.Pin_0, R12.Pin_0
  N14: R4.Pin_1, R5.Pin_0, R13.Pin_0
  N15: R5.Pin_1, R6.Pin_0, R14.Pin_0
  N16: R6.Pin_1, R7.Pin_0, R15.Pin_0
  N17: R7.Pin_1, R9.Pin_1, R16.Pin_0
  N18: C1.-, SP1.-
